// Logisim project AdderCircuits.circ as structural Verilog: 3 circuits, main circuit 8bitRippleCarryAdder
module halfAdder (
  input  A,
  input  B,
  output S,
  output C
);

  xor xor_1 (S, A, B);
  and and_1 (C, A, B);
endmodule

// FA
module fullAdder (
  input  A,
  input  B,
  input  Cin,
  output Cout,
  output S
);

  wire HA_1_c, HA_1_s, HA_2_c;

  or or_1 (Cout, HA_1_c, HA_2_c);
  halfAdder HA_1 (.A(A), .B(B), .S(HA_1_s), .C(HA_1_c));
  halfAdder HA_2 (.A(HA_1_s), .B(Cin), .S(S), .C(HA_2_c));
endmodule

module _8bitRippleCarryAdder (
  input  [7:0] A,
  input  [7:0] B,
  input  Cin,
  output Cout,
  output [7:0] S
);

  wire _0_cout, _1_cout, _2_cout, _3_cout, _4_cout, _5_cout, _6_cout;

  fullAdder _7 (.Cout(Cout), .A(A[7]), .B(B[7]), .S(S[7]), .Cin(_6_cout));
  fullAdder _6 (.Cout(_6_cout), .A(A[6]), .B(B[6]), .S(S[6]), .Cin(_5_cout));
  fullAdder _5 (.Cout(_5_cout), .A(A[5]), .B(B[5]), .S(S[5]), .Cin(_4_cout));
  fullAdder _4 (.Cout(_4_cout), .A(A[4]), .B(B[4]), .S(S[4]), .Cin(_3_cout));
  fullAdder _3 (.Cout(_3_cout), .A(A[3]), .B(B[3]), .S(S[3]), .Cin(_2_cout));
  fullAdder _2 (.Cout(_2_cout), .A(A[2]), .B(B[2]), .S(S[2]), .Cin(_1_cout));
  fullAdder _1 (.Cout(_1_cout), .A(A[1]), .B(B[1]), .S(S[1]), .Cin(_0_cout));
  fullAdder _0 (.Cout(_0_cout), .A(A[0]), .B(B[0]), .S(S[0]), .Cin(Cin));
endmodule
